# Fritzing sketch robot_arm_schematics (saved by Fritzing 0.9.3b)
breadboards: 1

parts:
  Part1 = Arduino Nano (Rev3.0)
  ElbowServo = Basic Servo
  ShoulderServo = Basic Servo
  RotationServo = Basic Servo
  U1 = Voltage Regulator - 5V [package="TO220 [THT]"]
  12V = Power plug
  C1 = Electrolytic Capacitor [capacitance=100µF package="100 mil [THT, electrolytic]"]

nets:
  GND: Part1.GND, ElbowServo.gnd, ShoulderServo.gnd, RotationServo.gnd, U1.GND, 12V.GND, C1.-
  N1: Part1.D3, RotationServo.pulse
  N2: Part1.D5, ShoulderServo.pulse
  N3: Part1.D6, ElbowServo.pulse
  VCC: Part1.5V, ElbowServo.vcc, ShoulderServo.vcc, RotationServo.vcc, U1.output_voltage, C1.+
  N4: U1.input_voltage, 12V.VCC
